// Logisim project DECODIFICADOR2x4.circ as structural Verilog: 1 circuit, main circuit main
module main (
  input  C1,
  input  C0,
  output S0,
  output S1,
  output S2,
  output S3
);

  wire not_1_out, not_2_out;

  not not_1 (not_1_out, C1);
  not not_2 (not_2_out, C0);
  and and_1 (S0, not_2_out, not_1_out);
  and and_2 (S1, not_1_out, C0);
  and and_3 (S2, C1, not_2_out);
  and and_4 (S3, C1, C0);

  // Notes on the sheet:
  //   C1: pull=up
  //   C0: pull=up
endmodule
