// Logisim project DEMUX1x4.circ as structural Verilog: 1 circuit, main circuit main
module main (
  input  C1,
  input  C0,
  input  Entada,
  output S0,
  output S1,
  output S2,
  output S3
);

  wire not_1_out, not_2_out;

  not not_1 (not_1_out, C1);
  not not_2 (not_2_out, C0);
  and and_1 (S0, Entada, not_2_out, not_1_out);
  and and_2 (S1, Entada, not_1_out, C0);
  and and_3 (S2, Entada, C1, not_2_out);
  and and_4 (S3, Entada, C1, C0);

  // Notes on the sheet:
  //   C1: pull=up
  //   C0: pull=up
endmodule
