// Logisim project MUX4x1.circ as structural Verilog: 1 circuit, main circuit main
module main (
  input  C1,
  input  C0,
  input  E0,
  input  E1,
  input  E2,
  input  E3,
  output \Saída 
);

  wire and_1_out, and_2_out, and_3_out, and_4_out, not_1_out, not_2_out;

  not not_1 (not_1_out, C1);
  not not_2 (not_2_out, C0);
  and and_1 (and_1_out, E0, not_2_out, not_1_out);
  and and_2 (and_2_out, E1, not_1_out, C0);
  and and_3 (and_3_out, E2, C1, not_2_out);
  and and_4 (and_4_out, E3, C1, C0);
  or or_1 (\Saída , and_1_out, and_2_out, and_3_out, and_4_out);

  // Notes on the sheet:
  //   E3: pull=down
  //   C0: pull=up
  //   C1: pull=up
endmodule
