// Logisim project PROCESSADOR.circ as structural Verilog: 1 circuit, main circuit main
module main (
  input  [1:0] Write_Reg,
  input  Write_Enable,
  input  [1:0] Read_RegA,
  input  [1:0] Read_RegB,
  input  F2,
  input  F1,
  input  F0,
  output [7:0] A,
  output [7:0] B,
  output [7:0] Write_Data
);

  wire and_1_out, and_2_out, and_3_out, and_4_out, CLK_out, decoder_1_out0, decoder_1_out1, decoder_1_out2,
       decoder_1_out3;
  wire [7:0] adder_1_out, adder_2_out, adder_3_out, and_5_out, or_1_out, R0_q, R1_q, R2_q, R3_q,
       subtractor_1_out;

  Decoder #(.select(2)) decoder_1 (
    .out0(decoder_1_out0), .out1(decoder_1_out1), .out2(decoder_1_out2), .out3(decoder_1_out3),
    .sel(Write_Reg), .en(CLK_out));
  and and_1 (and_1_out, decoder_1_out0, Write_Enable);
  and and_2 (and_2_out, decoder_1_out1, Write_Enable);
  and and_3 (and_3_out, decoder_1_out2, Write_Enable);
  and and_4 (and_4_out, decoder_1_out3, Write_Enable);
  Register #(.trigger("high")) R0 (.D(Write_Data), .en(CLK_out), .Q(R0_q), .clk(and_1_out));  // open: clr
  Register #(.trigger("high")) R1 (.D(Write_Data), .en(CLK_out), .Q(R1_q), .clk(and_2_out));  // open: clr
  Register #(.trigger("high")) R2 (.D(Write_Data), .en(CLK_out), .Q(R2_q), .clk(and_3_out));  // open: clr
  Register #(.trigger("high")) R3 (.D(Write_Data), .en(CLK_out), .Q(R3_q), .clk(and_4_out));  // open: clr
  Multiplexer #(.select(2), .width(8)) multiplexer_1 (
    .in0(R0_q), .in1(R1_q), .in2(R2_q), .in3(R3_q), .out(A), .sel(Read_RegA), .en(CLK_out));
  Multiplexer #(.select(2), .width(8)) multiplexer_2 (
    .in0(R0_q), .in1(R1_q), .in2(R2_q), .in3(R3_q), .out(B), .sel(Read_RegB), .en(CLK_out));
  Clock CLK (.out(CLK_out));
  Adder adder_1 (.a(A), .b(8'h1), .out(adder_1_out));  // open: cin, cout
  Adder adder_2 (.a(B), .b(8'h1), .out(adder_2_out));  // open: cin, cout
  Adder adder_3 (.a(A), .b(B), .out(adder_3_out));  // open: cin, cout
  Subtractor subtractor_1 (.a(A), .b(B), .out(subtractor_1_out));  // open: bin, bout
  assign and_5_out = A & B;  // AND_Gate and_5, 8 bits wide
  assign or_1_out = A | B;  // OR_Gate or_1, 8 bits wide
  Multiplexer #(.select(3), .width(8)) multiplexer_3 (
    .in0(A), .in1(B), .in2(adder_1_out), .in3(adder_2_out), .in4(adder_3_out), .in5(subtractor_1_out),
    .in6(and_5_out), .in7(or_1_out), .out(Write_Data), .sel({F2, F1, F0}), .en(CLK_out));

  // Notes on the sheet:
  //   Aluno: Lucas de Lima Castro MAT: 21551892
  //   Aluno: Levi Rodrigues de Almeida MAT: 21556276
  //   ULA:
  //   000: A
  //   001: B
  //   010: A +1
  //   011:B+1
  //   100: A + B
  //   101: A - B
  //   111:A or B
  //   110: A and B
endmodule
