// Logisim project SUBTRATOR.circ as structural Verilog: 5 circuits, main circuit meiosomador
module meiosomador (
  input  a,
  input  b,
  output s,
  output co
);

  wire not_1_out;

  not not_1 (not_1_out, a);
  xor xor_1 (s, a, b);
  and and_1 (co, not_1_out, b);
endmodule

module somadorcompleto (
  input  ci,
  input  a,
  input  b,
  output s,
  output co
);

  wire meiosomador_1_co, meiosomador_1_s, meiosomador_2_co;

  meiosomador meiosomador_1 (.a(a), .b(b), .s(meiosomador_1_s), .co(meiosomador_1_co));
  meiosomador meiosomador_2 (.a(ci), .b(meiosomador_1_s), .s(s), .co(meiosomador_2_co));
  or or_1 (co, meiosomador_2_co, meiosomador_1_co);
endmodule

module somador4bits (
  input  C0,
  input  A0,
  input  B0,
  input  A1,
  input  B1,
  input  A2,
  input  B2,
  input  A3,
  input  B3,
  output S0,
  output S1,
  output S2,
  output S3,
  output C4
);

  wire somadorcompleto_1_p4, somadorcompleto_2_p4, somadorcompleto_3_p4;

  // somadorcompleto somadorcompleto_1: pin names not known; wires that end beside it: C0, B0, A0, somadorcompleto_1_p4, S0, somadorcompleto_1_p4
  // somadorcompleto somadorcompleto_2: pin names not known; wires that end beside it: somadorcompleto_1_p4, B1, A1, somadorcompleto_2_p4, S1, somadorcompleto_2_p4
  // somadorcompleto somadorcompleto_3: pin names not known; wires that end beside it: somadorcompleto_2_p4, B2, A2, somadorcompleto_3_p4, S2, somadorcompleto_3_p4
  // somadorcompleto somadorcompleto_4: pin names not known; wires that end beside it: somadorcompleto_3_p4, B3, A3, S3, C4
endmodule

module somador8bits (
  input  C0,
  input  A0,
  input  B0,
  input  A1,
  input  B1,
  input  A2,
  input  B2,
  input  A3,
  input  B3,
  input  A4,
  input  B4,
  input  A5,
  input  B5,
  input  A6,
  input  B6,
  input  A7,
  input  B7,
  output out_18,
  output out_19,
  output out_20,
  output out_21,
  output out_22,
  output out_23,
  output out_24,
  output out_25,
  output out_26
);

  wire somador4bits_1_c4;

  somador4bits somador4bits_1 (
    .C0(C0), .A0(A0), .B0(B0), .A1(A1), .B1(B1), .A2(A2), .B2(B2), .A3(A3), .B3(B3), .S0(out_18),
    .S1(out_19), .S2(out_20), .S3(out_21), .C4(somador4bits_1_c4));
  somador4bits somador4bits_2 (
    .C0(somador4bits_1_c4), .A0(A4), .B0(B4), .A1(A5), .B1(B5), .A2(A6), .B2(B6), .A3(A7), .B3(B7),
    .S0(out_22), .S1(out_23), .S2(out_24), .S3(out_25), .C4(out_26));
endmodule

module subtrator (
  input  m,
  input  a0,
  input  b0,
  input  a1,
  input  b1,
  input  a2,
  input  b2,
  input  a3,
  input  b3,
  output s0,
  output s1,
  output s3,
  output s3_2,
  output out_14
);

  wire somadorcompleto_1_co, somadorcompleto_2_co, somadorcompleto_3_co, xor_1_out, xor_2_out, xor_3_out,
       xor_4_out;

  xor xor_1 (xor_1_out, b0, m);
  xor xor_2 (xor_2_out, b1, m);
  xor xor_3 (xor_3_out, b2, m);
  xor xor_4 (xor_4_out, b3, m);
  somadorcompleto somadorcompleto_1 (.ci(m), .a(a0), .b(xor_1_out), .s(s0), .co(somadorcompleto_1_co));
  somadorcompleto somadorcompleto_2 (
    .ci(somadorcompleto_1_co), .a(a1), .b(xor_2_out), .s(s1), .co(somadorcompleto_2_co));
  somadorcompleto somadorcompleto_3 (
    .ci(somadorcompleto_2_co), .a(a2), .b(xor_3_out), .s(s3), .co(somadorcompleto_3_co));
  somadorcompleto somadorcompleto_4 (.ci(somadorcompleto_3_co), .a(a3), .b(xor_4_out), .s(s3_2), .co(out_14));
endmodule
